// Logisim project ME7_Mendoza.circ as structural Verilog: 1 circuit, main circuit main
module main (
  input  clk,
  input  rst
);

  wire and_1_out, and_2_out, BEQ, BEQ1, BNE, BNE1, comparator_1_gt, comparator_1_lt, comparator_5_eq,
       comparator_5_gt, J1, or_1_out, s, w_en;
  wire [4:0] multiplexer_2_out;
  wire [5:0] adder_3_out, inst_mem_1_p2_2, reg_file_1_p12;
  wire [25:0] inst_mem_1_p2;
  wire [31:0] adder_1_out, adder_2_out, ALU_Out, bit_extender_1_out, bit_extender_2_out, bit_extender_3_out,
       Branch, JBranch, multiplexer_1_out, multiplexer_3_out, PC, rd1, rd2, reg_file_1_p11;

  or or_1 (or_1_out, J1, BEQ1, BNE1);
  // Probe on PC
  // Probe on ALU_Out
  not not_1 (w_en, or_1_out);
  // Probe on rd2
  // Probe on rd1
  Register #(.width(32)) register_1 (.D(multiplexer_3_out), .Q(PC), .clk(clk), .clr(rst));  // open: en
  // Probe on Branch
  Adder #(.width(32)) adder_1 (.a(32'h4), .b(PC), .out(adder_1_out));  // open: cin, cout
  Adder #(.width(32)) adder_2 (.a(Branch), .b(adder_1_out), .out(adder_2_out));  // open: cin, cout
  // INST_MEM inst_mem_1: pin names not known; wires that end beside it: PC, {inst_mem_1_p2_2, inst_mem_1_p2}
  Comparator #(.width(32)) comparator_1 (.a(rd1), .b(rd2), .gt(comparator_1_gt), .eq(BEQ), .lt(comparator_1_lt));
  assign bit_extender_1_out = {{6{inst_mem_1_p2[25]}}, inst_mem_1_p2};  // Bit_Extender bit_extender_1
  Multiplexer #(.width(32), .enable("false")) multiplexer_1 (
    .in0(adder_1_out), .in1(adder_2_out), .out(multiplexer_1_out), .sel(s));
  Comparator #(.width(6)) comparator_2 (.a(inst_mem_1_p2_2), .b(6'b000010), .eq(J1));  // open: gt, lt
  Comparator #(.width(6)) comparator_3 (.a(inst_mem_1_p2_2), .b(6'b000100), .eq(BEQ1));  // open: gt, lt
  Comparator #(.width(6)) comparator_4 (.a(inst_mem_1_p2_2), .b(6'b000101), .eq(BNE1));  // open: gt, lt
  and and_1 (and_1_out, BEQ1, BEQ);
  and and_2 (and_2_out, BNE1, BNE);
  Multiplexer #(.width(5), .enable("false")) multiplexer_2 (
    .in0(inst_mem_1_p2[20:16]), .in1(inst_mem_1_p2[15:11]), .out(multiplexer_2_out), .sel(comparator_5_eq));
  Comparator #(.width(6)) comparator_5 (
    .a(inst_mem_1_p2_2), .b({6{1'b0}}), .gt(comparator_5_gt), .eq(comparator_5_eq));  // open: lt
  // Probe on multiplexer_1_out
  // Probe on JBranch
  // Probe on multiplexer_2_out
  assign bit_extender_2_out = {{16{inst_mem_1_p2[15]}}, inst_mem_1_p2[15:0]};  // Bit_Extender bit_extender_2
  or or_2 (s, and_1_out, and_2_out);
  Multiplexer #(.width(32), .enable("false")) multiplexer_3 (
    .in0(multiplexer_1_out), .in1(JBranch), .out(multiplexer_3_out), .sel(J1));
  // Probe on J1
  // Probe on inst_mem_1_p2[25:21]
  Shifter #(.width(32)) shifter_1 (.in(bit_extender_2_out), .\dist (5'b00010), .out(Branch));
  // Probe on BNE
  or or_3 (BNE, comparator_1_gt, comparator_1_lt);
  // Probe on BEQ
  // Probe on multiplexer_3_out
  assign bit_extender_3_out = {{16{inst_mem_1_p2[15]}}, inst_mem_1_p2[15:0]};  // Bit_Extender bit_extender_3
  // REG_FILE reg_file_1: pin names not known; wires that end beside it: inst_mem_1_p2[25:21], inst_mem_1_p2[20:16], multiplexer_2_out, ALU_Out, w_en, clk, rst, rd1, rd2, rd1, reg_file_1_p11, reg_file_1_p12
  Shifter #(.width(32)) shifter_2 (.in(bit_extender_1_out), .\dist (5'b00010), .out(JBranch));
  Multiplexer #(.width(32), .enable("false")) multiplexer_4 (
    .in0(rd2), .in1(bit_extender_3_out), .out(reg_file_1_p11), .sel(comparator_5_gt));
  Multiplexer #(.width(6), .enable("false")) multiplexer_5 (
    .in0(inst_mem_1_p2[5:0]), .in1(adder_3_out), .out(reg_file_1_p12), .sel(comparator_5_gt));
  Adder #(.width(6)) adder_3 (.a(inst_mem_1_p2_2), .b(6'b011000), .out(adder_3_out));  // open: cin, cout
  // Probe on inst_mem_1_p2[5:0]
  // Probe on reg_file_1_p12
  // Probe on adder_3_out
  // Probe on comparator_5_gt
  // ALU alu_1: pin names not known; wires that end beside it: ALU_Out
  // Probe on ALU_Out
endmodule
