// Logisim project ME8_Mendoza.circ as structural Verilog: 1 circuit, main circuit main
module main (
  input  rst
);

  wire and_1_out, and_2_out, BEQ, BEQ1, BNE, BNE1, clk, comparator_6_eq, comparator_6_gt, comparator_7_gt,
       comparator_7_lt, J1, LW1, or_1_out, s, SW1, w_en;
  wire [4:0] multiplexer_2_out;
  wire [5:0] adder_4_out, inst_mem_1_p2_2, reg_file_1_p9;
  wire [25:0] inst_mem_1_p2;
  wire [31:0] adder_1_out, adder_2_out, adder_3_out, ALU_Out, bit_extender_1_out, bit_extender_2_out,
       bit_extender_3_out, bit_extender_4_out, Branch, data_out, JBranch, multiplexer_1_out,
       multiplexer_3_out, PC, rd1, rd2, reg_file_1_p8, write_data;

  Clock u_clk (.out(clk));
  or or_1 (or_1_out, J1, BEQ1, SW1, BNE1);
  assign bit_extender_1_out = {{16{inst_mem_1_p2[15]}}, inst_mem_1_p2[15:0]};  // Bit_Extender bit_extender_1
  // Probe on PC
  // Probe on ALU_Out
  not not_1 (w_en, or_1_out);
  Register #(.width(32)) register_1 (.D(multiplexer_3_out), .Q(PC), .clk(clk), .clr(rst));  // open: en
  // Probe on Branch
  Adder #(.width(32)) adder_1 (.a(32'h4), .b(PC), .out(adder_1_out));  // open: cin, cout
  Adder #(.width(32)) adder_2 (.a(rd1), .b(bit_extender_1_out), .out(adder_2_out));  // open: cin, cout
  Adder #(.width(32)) adder_3 (.a(Branch), .b(adder_1_out), .out(adder_3_out));  // open: cin, cout
  // INST_MEM inst_mem_1: pin names not known; wires that end beside it: PC, {inst_mem_1_p2_2, inst_mem_1_p2}
  assign bit_extender_2_out = {{6{inst_mem_1_p2[25]}}, inst_mem_1_p2};  // Bit_Extender bit_extender_2
  // Probe on data_out
  Multiplexer #(.width(32), .enable("false")) multiplexer_1 (
    .in0(adder_1_out), .in1(adder_3_out), .out(multiplexer_1_out), .sel(s));
  Comparator #(.width(6)) comparator_1 (.a(inst_mem_1_p2_2), .b(6'b000010), .eq(J1));  // open: gt, lt
  Comparator #(.width(6)) comparator_2 (.a(inst_mem_1_p2_2), .b(6'b000100), .eq(BEQ1));  // open: gt, lt
  Comparator #(.width(6)) comparator_3 (.a(inst_mem_1_p2_2), .b(6'b000101), .eq(BNE1));  // open: gt, lt
  Comparator #(.width(6)) comparator_4 (.a(inst_mem_1_p2_2), .b(6'b100011), .eq(LW1));  // open: gt, lt
  Comparator #(.width(6)) comparator_5 (.a(inst_mem_1_p2_2), .b(6'b101011), .eq(SW1));  // open: gt, lt
  // Probe on adder_2_out
  // Probe on SW1
  and and_1 (and_1_out, BEQ1, BEQ);
  and and_2 (and_2_out, BNE1, BNE);
  Multiplexer #(.width(5), .enable("false")) multiplexer_2 (
    .in0(inst_mem_1_p2[20:16]), .in1(inst_mem_1_p2[15:11]), .out(multiplexer_2_out), .sel(comparator_6_eq));
  Comparator #(.width(6)) comparator_6 (
    .a(inst_mem_1_p2_2), .b({6{1'b0}}), .gt(comparator_6_gt), .eq(comparator_6_eq));  // open: lt
  // Probe on rd2
  // Probe on inst_mem_1_p2[20:16]
  // Probe on multiplexer_2_out
  assign bit_extender_3_out = {{16{inst_mem_1_p2[15]}}, inst_mem_1_p2[15:0]};  // Bit_Extender bit_extender_3
  or or_2 (s, and_1_out, and_2_out);
  Multiplexer #(.width(32), .enable("false")) multiplexer_3 (
    .in0(multiplexer_1_out), .in1(JBranch), .out(multiplexer_3_out), .sel(J1));
  // Probe on inst_mem_1_p2[25:21]
  Shifter #(.width(32)) shifter_1 (.in(bit_extender_3_out), .\dist (5'b00010), .out(Branch));
  // DATA_MEM data_mem_1: pin names not known; wires that end beside it: adder_2_out, rd2, SW1, clk, rst, data_out
  assign bit_extender_4_out = {{16{inst_mem_1_p2[15]}}, inst_mem_1_p2[15:0]};  // Bit_Extender bit_extender_4
  Comparator #(.width(32)) comparator_7 (.a(rd1), .b(rd2), .gt(comparator_7_gt), .eq(BEQ), .lt(comparator_7_lt));
  // REG_FILE reg_file_1: pin names not known; wires that end beside it: inst_mem_1_p2[25:21], inst_mem_1_p2[20:16], multiplexer_2_out, write_data, rd1, rd2, rd1, reg_file_1_p8, reg_file_1_p9
  Shifter #(.width(32)) shifter_2 (.in(bit_extender_2_out), .\dist (5'b00010), .out(JBranch));
  // Probe on rd2
  Multiplexer #(.width(32), .enable("false")) multiplexer_4 (
    .in0(rd2), .in1(bit_extender_4_out), .out(reg_file_1_p8), .sel(comparator_6_gt));
  Multiplexer #(.width(6), .enable("false")) multiplexer_5 (
    .in0(inst_mem_1_p2[5:0]), .in1(adder_4_out), .out(reg_file_1_p9), .sel(comparator_6_gt));
  Adder #(.width(6)) adder_4 (.a(inst_mem_1_p2_2), .b(6'b011000), .out(adder_4_out));  // open: cin, cout
  // Probe on inst_mem_1_p2[5:0]
  // Probe on reg_file_1_p9
  // Probe on adder_4_out
  // Probe on comparator_6_gt
  or or_3 (BNE, comparator_7_gt, comparator_7_lt);
  // ALU alu_1: pin names not known; wires that end beside it: ALU_Out
  // Probe on data_out
  // Probe on write_data
  Multiplexer #(.width(32), .enable("false")) multiplexer_6 (
    .in0(ALU_Out), .in1(data_out), .out(write_data), .sel(LW1));
  // Probe on LW1
endmodule
